# Fritzing sketch Temperature Sketch (saved by Fritzing 0.9.2b)
breadboards: 1

parts:
  Parte1 = Arduino Uno (Rev3)
  DHT1 = DHT11 Humitidy and Temperature Sensor
  R1 = Resistor [tolerance=±5% resistance=220 package=THT]

nets:
  5V: Parte1.5V, DHT1.VDD
  GND: Parte1.GND, DHT1.GND
  N1: DHT1.DATA, R1.Pin_1

custom parts:
  DHT11 Humitidy and Temperature Sensor: DHT11 Humidity and Temperature Sensor
